// Logisim project TP 1.circ as structural Verilog: 1 circuit, main circuit main
module main (
  input  D,
  input  C,
  input  B,
  input  A,
  output S
);

  wire and_1_out, and_2_out, and_3_out;

  and and_1 (and_1_out, B, A);
  and and_2 (and_2_out, C, A);
  and and_3 (and_3_out, D, C, B);
  or or_1 (S, and_1_out, and_2_out, and_3_out);
endmodule
