// Logisim project TP 2.circ as structural Verilog: 1 circuit, main circuit main
module main (
  input  A,
  input  B,
  input  C,
  input  D,
  output S
);

  wire and_1_out, and_2_out, and_3_out, and_4_out, and_5_out, and_6_out, and_7_out, not_1_out, not_2_out,
       not_3_out, not_4_out, not_5_out, not_6_out, not_7_out, not_8_out;

  not not_1 (not_1_out, C);
  not not_2 (not_2_out, D);
  not not_3 (not_3_out, B);
  not not_4 (not_4_out, D);
  not not_5 (not_5_out, D);
  not not_6 (not_6_out, C);
  not not_7 (not_7_out, B);
  not not_8 (not_8_out, A);
  and and_1 (and_1_out, A, B, not_1_out, not_2_out);
  and and_2 (and_2_out, A, not_3_out, C, not_4_out);
  and and_3 (and_3_out, A, B, C, not_5_out);
  and and_4 (and_4_out, A, B, not_6_out, D);
  and and_5 (and_5_out, A, not_7_out, C, D);
  and and_6 (and_6_out, not_8_out, B, C, D);
  and and_7 (and_7_out, A, B, C, D);
  or or_1 (S, and_1_out, and_2_out, and_3_out, and_4_out, and_5_out, and_6_out, and_7_out);
endmodule
