// Logisim project TP 3.circ as structural Verilog: 1 circuit, main circuit main
module main (
  input  P,
  input  L,
  input  W,
  input  H,
  output A,
  output B,
  output C
);

  wire and_1_out, and_2_out, and_3_out, and_4_out, and_5_out, and_6_out, and_7_out, and_8_out, and_9_out,
       and_10_out, not_1_out, not_2_out, not_3_out, not_4_out, not_5_out, not_6_out, not_7_out, not_8_out,
       not_9_out, not_10_out, not_11_out, not_12_out, not_13_out;

  not not_1 (not_1_out, P);
  not not_2 (not_2_out, W);
  not not_3 (not_3_out, H);
  not not_4 (not_4_out, L);
  not not_5 (not_5_out, H);
  not not_6 (not_6_out, L);
  not not_7 (not_7_out, W);
  not not_8 (not_8_out, P);
  not not_9 (not_9_out, L);
  not not_10 (not_10_out, P);
  not not_11 (not_11_out, W);
  not not_12 (not_12_out, P);
  not not_13 (not_13_out, H);
  and and_1 (and_1_out, P, L, W);
  and and_2 (and_2_out, P, L, H);
  and and_3 (and_3_out, P, W, H);
  and and_4 (and_4_out, not_1_out, L, W, H);
  and and_5 (and_5_out, P, not_2_out, not_3_out);
  and and_6 (and_6_out, P, not_4_out, not_5_out);
  and and_7 (and_7_out, P, not_6_out, not_7_out);
  and and_8 (and_8_out, not_8_out, not_9_out);
  and and_9 (and_9_out, not_10_out, not_11_out);
  and and_10 (and_10_out, not_12_out, not_13_out);
  or or_1 (A, and_1_out, and_2_out, and_3_out);
  or or_2 (B, and_4_out, and_5_out, and_6_out, and_7_out);
  or or_3 (C, and_8_out, and_9_out, and_10_out);
endmodule
