// Logisim project TP 4.circ as structural Verilog: 1 circuit, main circuit main
module main (
  input  [7:0] in_1,
  input  [7:0] in_2,
  input  [7:0] in_3,
  input  [7:0] in_4,
  input  [7:0] in_5,
  input  [7:0] in_6,
  input  [7:0] in_7,
  input  [7:0] in_8,
  input  [7:0] in_9,
  input  [7:0] in_10,
  input  [7:0] in_11,
  input  [2:0] in_12,
  input  [1:0] in_13,
  input  [7:0] in_14,
  output [7:0] out_15,
  output [7:0] out_16
);

  wire clock_1_out, d_ff_1_q, d_ff_1_qn, d_ff_2_q, d_ff_2_qn;

  Clock clock_1 (.out(clock_1_out));
  D_Flip_Flop d_ff_1 (.clk(clock_1_out), .D(d_ff_1_qn), .Q(d_ff_1_q), .Qn(d_ff_1_qn));  // open: preset, reset
  Multiplexer #(.select(2), .width(8), .enable("false")) multiplexer_1 (
    .in0(in_3), .in1(in_6), .in2(in_8), .in3(in_10), .out(out_16), .sel(in_13));
  D_Flip_Flop d_ff_2 (.clk(d_ff_1_q), .D(d_ff_2_qn), .Q(d_ff_2_q), .Qn(d_ff_2_qn));  // open: preset, reset
  // Digital_Oscilloscope digital_oscilloscope_1: pin names not known; wires that end beside it: clock_1_out, d_ff_1_q, d_ff_1_qn, d_ff_2_q
  Multiplexer #(.select(3), .width(8), .enable("false")) multiplexer_2 (
    .in0(in_1), .in1(in_2), .in2(in_4), .in3(in_5), .in4(in_7), .in5(in_9), .in6(in_11), .in7(in_14),
    .out(out_15), .sel(in_12));
endmodule
