// Logisim project TP 5.circ as structural Verilog: 1 circuit, main circuit main
module main (
  input  [7:0] in_1,
  input  [7:0] in_2,
  input  [7:0] in_3,
  input  [7:0] in_4,
  input  [1:0] in_5,
  input  [7:0] in_6,
  input  [7:0] in_7,
  input  [7:0] in_8,
  input  [7:0] in_9,
  input  [7:0] in_10,
  input  [7:0] in_11,
  input  [7:0] in_12,
  input  [2:0] in_13,
  input  [7:0] in_14,
  output [7:0] out_15,
  output [7:0] out_16
);

  Multiplexer #(.select(2), .width(8), .enable("false")) multiplexer_1 (
    .in0(in_1), .in1(in_2), .in2(in_3), .in3(in_4), .out(out_15), .sel(in_5));
  Multiplexer #(.select(3), .width(8), .enable("false")) multiplexer_2 (
    .in0(in_6), .in1(in_7), .in2(in_8), .in3(in_9), .in4(in_10), .in5(in_11), .in6(in_12), .in7(in_14),
    .out(out_16), .sel(in_13));
endmodule
